# Fritzing sketch RFM69ESP8266 (saved by Fritzing 0.9.3b)
circuit board: 7.32425cm x 4.90436cm
breadboards: 1

parts:
  J3 = female pin header, 8 pins [form="♀ (female)"]
  J4 = female pin header, 8 pins [form="♀ (female)"]
  R1 = Resistor [tolerance=±5% resistance=10k package=THT]
  U2 = TLP621 [package=THT]
  R3 = Resistor [tolerance=±5% resistance=10k package=THT]
  EAU = female pin header, 2 pins [form="♀ (female)"]
  GAZ = female pin header, 2 pins [form="♀ (female)"]
  J6 = double row female pin header, 30 pins [form="♀ (female)"]
  J7 = double row female pin header, 30 pins [form="♀ (female)"]
  EDF = screw terminal, 2 pins
  J8 = female pin header, 1 pin [form="♀ (female)"]
  R2 = Resistor [tolerance=±5% resistance=1.5k package=THT]
  R4 = Resistor [tolerance=±5% resistance=3.3k package=THT]
  5V_IN = screw terminal, 2 pins
  J9 = female pin header, 3 pins [form="♀ (female)"]

nets:
  N1: J3.pin1, EAU.pin1, GAZ.pin2, J7.pin6, J7.pin25, R4.Pin_0, J9.pin2
  N2: J3.pin7, J7.pin28
  N3: J4.pin2, J8.pin1
  N4: J4.pin3, R1.Pin_0, R3.Pin_0, J7.pin24, J9.pin3
  N5: J4.pin4, J7.pin23
  N6: J4.pin5, J7.pin22
  N7: J4.pin6, J7.pin21
  N8: J4.pin7, J7.pin20
  N9: R1.Pin_1, GAZ.pin1, J7.pin27
  N10: U2.Pin_1, R2.Pin_1
  N11: U2.Pin_2, EDF.pin1
  N12: U2.Pin_4, J7.pin12, J7.pin19, R4.Pin_1
  N13: U2.Pin_3, J6.pin10, J6.pin21
  N14: R3.Pin_1, EAU.pin2, J7.pin29
  N15: J6.pin14, 5V_IN.pin2
  N16: J6.pin15, 5V_IN.pin1
  N17: J7.pin26, J9.pin1
  N18: EDF.pin2, R2.Pin_0

notes:
  +
  -
  eau
  gaz
  EDF
