# Fritzing sketch RFM69ESP8266_v2 (saved by Fritzing 0.9.3b)
circuit board: 8.49104cm x 5.02923cm
breadboards: 1

parts:
  J3 = female pin header, 8 pins [form="♀ (female)"]
  J4 = female pin header, 8 pins [form="♀ (female)"]
  R1 = Resistor [tolerance=±5% resistance=6.8k package=THT]
  GAZ = female pin header, 2 pins [form="♀ (female)"]
  J6 = double row female pin header, 30 pins [form="♀ (female)"]
  J7 = double row female pin header, 30 pins [form="♀ (female)"]
  EDF = screw terminal, 2 pins
  J8 = female pin header, 1 pin [form="♀ (female)"]
  J9 = female pin header, 3 pins [form="♀ (female)"]
  U3 = TLP621 [package=THT]
  R5 = Resistor [tolerance=±5% resistance=10k package=THT]
  R6 = Resistor [tolerance=±5% resistance=3.3k package=THT]
  220_V = screw terminal, 2 pins
  J10 = female pin header, 3 pins [form="♀ (female)"]
  J11 = female pin header, 5 pins [form="♀ (female)"]

nets:
  N1: J3.pin1, GAZ.pin2, J7.pin6, J7.pin25, J9.pin2, R5.Pin_0
  N2: J3.pin7, J7.pin28
  N3: J4.pin2, J8.pin1
  N4: J4.pin3, R1.Pin_0, J7.pin7, J7.pin24, J9.pin3, U3.Pin_3
  N5: J4.pin4, J7.pin23
  N6: J4.pin5, J7.pin22
  N7: J4.pin6, J7.pin21
  N8: J4.pin7, J7.pin20
  N9: R1.Pin_1, GAZ.pin1, J7.pin27
  N10: J6.pin10, J6.pin21
  N11: J6.pin14, J11.pin5
  N12: J6.pin15, J6.pin16, J11.pin1
  N13: J7.pin2, J7.pin29, U3.Pin_4, R5.Pin_1
  N14: J7.pin12, J7.pin19
  N15: J7.pin26, J9.pin1
  N16: EDF.pin1, R6.Pin_0
  N17: EDF.pin2, U3.Pin_1
  N18: U3.Pin_2, R6.Pin_1
  N19: 220_V.pin1, J10.pin1
  N20: 220_V.pin2, J10.pin3

notes:
  5v
  -
  gaz
  EDF
  +
  220V
