# Fritzing sketch ESP8266GAZ (saved by Fritzing 0.9.3b)
circuit board: 4.34622cm x 3.95111cm
breadboards: 1

parts:
  J1 = female pin header, 6 pins [form="♀ (female)"]
  R1 = Resistor [tolerance=±5% resistance=220 package=THT]
  R2 = Resistor [tolerance=±5% resistance=10k package=THT]
  LED1 = LED - 5mm [color="Red (633nm)" package="5 mm [THT]"]
  J2 = female pin header, 2 pins [form="♀ (female)"]
  Pad16 = Pad [width=5.0058320000000176 height=1.2478270095238149 connect=center]  # not connected
  Pad15 = Pad [width=5.0058320000000176 height=1.2478270095238149 connect=center]  # not connected
  Pad14 = Pad [width=5.0058320000000176 height=1.2478270095238149 connect=center]  # not connected
  Pad13 = Pad [width=5.0058320000000176 height=1.2478270095238149 connect=center]  # not connected
  Pad12 = Pad [width=5.0058320000000176 height=1.2478270095238149 connect=center]  # not connected
  Pad11 = Pad [width=5.0058320000000176 height=1.2478270095238149 connect=center]
  Pad10 = Pad [width=5.0058320000000176 height=1.2478270095238149 connect=center]
  Pad9 = Pad [width=5.0058320000000176 height=1.2478270095238149 connect=center]  # not connected
  Pad8 = Pad [width=5.0058320000000176 height=1.2478270095238149 connect=center]
  Pad7 = Pad [width=5.0058320000000176 height=1.2478270095238149 connect=center]
  Pad6 = Pad [width=5.0058320000000176 height=1.2478270095238149 connect=center]
  Pad5 = Pad [width=5.0058320000000176 height=1.2478270095238149 connect=center]
  Pad4 = Pad [width=5.0058320000000176 height=1.2478270095238149 connect=center]  # not connected
  Pad3 = Pad [width=5.0058320000000176 height=1.2478270095238149 connect=center]
  Pad2 = Pad [width=5.0058320000000176 height=1.2478270095238149 connect=center]
  Pad1 = Pad [width=5.0058320000000176 height=1.2478270095238149 connect=center]
  R3 = Resistor [tolerance=±5% resistance=10k package=THT]
  R4 = Resistor [tolerance=±5% resistance=10k package=THT]
  R5 = Resistor [tolerance=±5% resistance=10k package=THT]
  Q1 = Basic FET P-Channel [package="TO220 [THT]"]
  Pad17 = Pad [width=2.3142222222222411 height=3.3866666666666587 connect=center]
  Pad18 = Pad [width=2.3142222222222411 height=3.3866666666666587 connect=center]
  C1 = Electrolytic Capacitor [capacitance=1µF package="100 mil [THT, electrolytic]"]
  C2 = Electrolytic Capacitor [capacitance=1µF package="100 mil [THT, electrolytic]"]

nets:
  N1: J1.pin2, Pad1.pad
  N2: J1.pin3, Pad2.pad
  N3: J1.pin4, J2.pin2, Pad11.pad, R3.Pin_1, R4.Pin_0, Q1.drain, C1.+
  N4: J1.pin6, R1.Pin_0, R2.Pin_0, Pad8.pad, R5.Pin_0, Q1.gate, Pad17.pad, C1.-, C2.-
  N5: R1.Pin_1, LED1.cathode
  N6: R2.Pin_1, J2.pin1, Pad6.pad
  N7: LED1.anode, Pad3.pad
  N8: Pad10.pad, R3.Pin_0
  N9: Pad7.pad, R5.Pin_1
  N10: Pad5.pad, R4.Pin_1
  N11: Q1.source, Pad18.pad, C2.+

notes:
  +
  -
